# Fritzing sketch electronic_level (saved by Fritzing 1.0.8)
breadboards: 1

parts:
  U1 = LuaNode32 / ESP32 [part_number=ESP32S-PIN30]
  A1 = GC9A01 round lcd
  A2 = BMI160 breakout
  S1 = Pushbutton [package="[SMD]"]

nets:
  N1: U1.GND, U1.D4, A1.Pin_6, A2.Pin_8, A2.Pin_12, S1.Pin_1, S1.Pin_2, S1.Pin_3, S1.Pin_4
  N2: U1.3V3, A1.Pin_7, A2.Pin_7, A2.Pin_11
  N3: U1.RX2, A1.Pin_1
  N4: U1.TX2, A1.Pin_3
  N5: U1.D5, A1.Pin_2
  N6: U1.D18, A1.Pin_5
  N7: U1.D21, A2.Pin_10
  N8: U1.D22, A2.Pin_9
  N9: U1.D23, A1.Pin_4

custom parts:
  LuaNode32 / ESP32: New Image for LuaNode32 DOIT ESP32 DEVKIT V1. Base parts from LuaNode32 / ESP32 ESP32 based LuaNode32 by G.Noorlander DOIT Esp32 DevKit v1 (30 pins long, 11 pins width) by Werner Rothschopf (modified by vanepp Dec 2018)
  GC9A01 round lcd: IPS TFT display round 1.28″ 240×240 GC9A01 controller. Mar 2025 fix pcb pin with fill #ffffff instead of none. Casuses problem in etchable pcb images (pad with no hole.)
  BMI160 breakout: BMI160 Latest Stance Accelerometer Gyroscope module 6 Dof inertial Measurement Sensors.
